# Fritzing sketch So do (saved by Fritzing 0.9.3b)

parts:
  U1 = NodeMCU V1.0
  L298N1 = L298N DC motor driver
  M2 = DC Motor
  M3 = DC Motor
  M4 = DC Motor
  M1 = DC Motor
  J1 = Basic Servo
  J2 = Basic Servo
  BAT1 = 18650 battery holder [package=battery-18650-kit]
  BAT3 = 18650 battery holder [package=battery-18650-kit]
  BAT4 = 18650 battery holder [package=battery-18650-kit]
  BAT5 = 18650 battery holder [package=battery-18650-kit]
  U2 = LM2596 step down module

nets:
  N1: U1.D0, J2.pulse
  N2: U1.D2, L298N1.ENA
  N3: U1.D3, L298N1.IN1
  N4: U1.D4, L298N1.IN2
  GND: U1.GND, L298N1.GND, J1.gnd, J2.gnd, BAT1.-, U2.IN-, U2.OUT-
  N5: U1.D5, J1.pulse
  N6: U1.D6, L298N1.IN3
  N7: U1.D7, L298N1.IN4
  N8: U1.D8, L298N1.ENB
  VIN: U1.Vin, L298N1.5V
  N9: L298N1.OUT1, M3.pin_2, M4.pin_2
  N10: L298N1.OUT2, M3.pin_1, M4.pin_1
  N11: L298N1.OUT3, M2.pin_2, M1.pin_2
  N12: L298N1.OUT4, M2.pin_1, M1.pin_1
  N13: L298N1.12V, BAT5.+, U2.IN+
  VCC: J1.vcc, J2.vcc, U2.OUT+
  N14: BAT1.+, BAT4.-
  N15: BAT3.+, BAT5.-
  N16: BAT3.-, BAT4.+

notes:
  gripper
  Arm

custom parts:
  NodeMCU V1.0: ESP8266 based NodeMCU
  L298N DC motor driver: 2x DC motor driver with 78M05 positive voltage regulator (7..35 V) L298N: max 46 V, 2 A Set 5 V Enable jumper to enable 5 V regultor (needed for the L298N) and +5 V output at screw terminal or supply external +5 V at screw terminal Set ENA and/or ENB to +5 V to enable motor permanently or supply ENA and/or ENB with PWM signal IN1 and IN2 set rotation directory for motor A (OUT1/OUT2) IN2 and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
  18650 battery holder: 18650 Battery Holder
  LM2596 step down module: LM2596 DC-DC step down power supply module 3 A.
