# Fritzing sketch Untitled Sketch 4 (saved by Fritzing 0.9.3b)
circuit board: 14.4197cm x 7.18291cm
breadboards: 1

parts:
  Part1 = Arduino Uno (Rev3) - ICSP
  Part2 = NRF24L01+ Breakout Board
  C1 = Capacitor Polarized [package=cpol-radial-10uf-25v]

nets:
  N1: Part1.ICSP_MISO, Part2.MISO
  N2: Part1.ICSP_SCK, Part2.SCK
  N3: Part1.ICSP_MOSI, Part2.MOSI
  GND: Part1.GND, Part2.GND, C1.-
  N4: Part1.D8, Part2.CS
  N5: Part1.D7, Part2.CE
  3V3: Part1.3V3, Part2.VCC, C1.+
